# Fritzing sketch schematics (saved by Fritzing 0.9.1b)
circuit board: 17.1895cm x 6.0818cm

parts:
  DC_motor = DC Motor
  MOSFET = MOSFET-NCHANNEL [package=to220v]
  DIODE = Diode [package=diode-1n4001]
  Pot_22K = POT [package=pot_mammoth]
  Gas_Sensor = GAS_SENSOR [package=mq-3]
  LED1 = 8x8 LED Matrix (blue)
  Arduino_UNO = Arduino Uno (Rev3) - ICSP
  R1 = Resistor [tolerance=±5% resistance=1k package="0603 [SMD]"]
  button = SWITCH-MOMENTARY-2 [package=tactile-pth-12mm]

nets:
  N1: DC_motor.pin_1, DIODE.C, Arduino_UNO.VIN
  G: DC_motor.pin_2, MOSFET.G, DIODE.A
  S: MOSFET.D, Arduino_UNO.D3_PWM, R1.Pin_1
  D: MOSFET.S, Pot_22K.A, Gas_Sensor.H2, LED1.-, Arduino_UNO.GND, R1.Pin_0, button.2
  N2: Pot_22K.S, Gas_Sensor.B1, Arduino_UNO.A0
  N3: Pot_22K.E, Gas_Sensor.A1, Gas_Sensor.H1, LED1.+, Arduino_UNO.5V
  N4: LED1.D, Arduino_UNO.ICSP_MOSI, Arduino_UNO.D11_PWM/MOSI
  N5: LED1.C, Arduino_UNO.A5/SCL
  N6: Arduino_UNO.D4, button.1

custom parts:
  8x8 LED Matrix (blue): 8x8 LED Matrix with I2C control (blue)
